# Fritzing sketch Button (saved by Fritzing 0.9.3b)
breadboards: 1

parts:
  Part1 = Arduino Nano (Rev3.0)
  S1 = Momentary Switch [package=ksa_sealed_tac_switch]
  R5 = Resistor [tolerance=±5% resistance=10k package="1206 [SMD]"]

nets:
  N1: Part1.GND, S1.3
  N2: Part1.D2, S1.2, R5.Pin_1
  N3: Part1.5V, R5.Pin_0
