# Fritzing sketch Led (saved by Fritzing 0.9.3b)
breadboards: 1

parts:
  Part1 = Arduino Nano (Rev3.0)
  LED1 = LED - 5mm [color="Red (633nm)" package="5 mm [THT]"]
  R1 = Resistor [tolerance=±5% resistance=330 package="0402 [SMD]"]

nets:
  N1: Part1.GND, R1.Pin_1
  N2: Part1.D3, LED1.anode
  N3: LED1.cathode, R1.Pin_0
