# Fritzing sketch LedButtonPhotoResistor (saved by Fritzing 0.9.3b)
breadboards: 1

parts:
  Part1 = Arduino Nano (Rev3.0)
  LED1 = LED - 5mm [color="Red (633nm)" package="5 mm [THT]"]
  R1 = Resistor [tolerance=±5% resistance=330 package="0402 [SMD]"]
  R3 = Resistor [tolerance=±5% resistance=10k package="1206 [SMD]"]
  R4 = Photocell (LDR) [package=THT]
  R5 = Resistor [tolerance=±5% resistance=10k package="1206 [SMD]"]
  S1 = Momentary Switch [package=ksa_sealed_tac_switch]

nets:
  N1: Part1.GND, R1.Pin_1, R3.Pin_1, S1.3
  N2: Part1.D2, R5.Pin_1, S1.2
  N3: Part1.D3, LED1.anode
  N4: Part1.5V, R4.pin_1, R5.Pin_0
  N5: Part1.A0, R3.Pin_0, R4.pin_0
  N6: LED1.cathode, R1.Pin_0
