# Fritzing sketch PhotoResistor (saved by Fritzing 0.9.3b)
breadboards: 1

parts:
  Part1 = Arduino Nano (Rev3.0)
  R4 = Photocell (LDR) [package=THT]
  R3 = Resistor [tolerance=±5% resistance=10k package="1206 [SMD]"]

nets:
  N1: Part1.GND, R3.Pin_1
  N2: Part1.5V, R4.pin_1
  N3: Part1.A0, R4.pin_0, R3.Pin_0
